# Fritzing sketch Combined_Sketch (saved by Fritzing 0.9.5d)
breadboards: 2

parts:
  M5 = DOIT Esp32 DevKit v1 (30 pins long, 11 pins width) [part_number=ESP32S-PIN30]
  HC-SR04_Sensor_2 = HC-SR04 Ultrasonic Distance Sensor
  VCC2 = Battery
  DHT2 = DHT11 Humitidy and Temperature Sensor (3 pins)
  DS3 = DS18B20 1-Wire Temperature Sensor Probe
  R4 = Resistor [tolerance=±5% resistance=4.7 package="2010 [SMD]"]
  R6 = Resistor [tolerance=±5% resistance=10 package="2010 [SMD]"]
  R8 = Photocell (LDR) [package=THT]
  M6 = PH meter with sensor in breadboard [package=THT]
  A3 = tds-sensor-meter-v1.0_1
  M9 = 1 chan 5v relay module
  WATER_PUMP3 = water pump/motor

nets:
  N1: M5.D4, DHT2.Plus
  N2: M5.D5, HC-SR04_Sensor_2.TRIG
  N3: M5.D18, HC-SR04_Sensor_2.ECHO
  N4: M5.D34, R6.Pin_0, R8.pin_1
  N5: M5.D35, M6.pin3
  N6: M5.D32, A3.pin1
  N7: M5.D26, M9.pin_3
  N8: M5.D13, DS3.DQ, R4.Pin_1
  VCC: HC-SR04_Sensor_2.VCC, VCC2.+, DHT2.Signal, DS3.VDD, R8.pin_0, M6.pin1, A3.pin2, M9.pin_1, M9.pin_4
  GND: HC-SR04_Sensor_2.GND, VCC2.-, DHT2.Gnd, DS3.GND, R4.Pin_0, R6.Pin_1, M6.pin2, A3.pin3, M9.pin_2, WATER_PUMP3.pin_1
  N9: M9.pin_5, WATER_PUMP3.pin_2

custom parts:
  DOIT Esp32 DevKit v1 (30 pins long, 11 pins width): The DOIT Esp32 DevKit v1 is one of the development board created by DOIT to evaluate the ESP-WROOM-32 module. It is based on the ESP32 microcontroller that boasts Wifi, Bluetooth, Ethernet and Low Power support all in a single chip. (vanepp) made breadboard work, adjusted pin numbering and labels and reduced size of schematic and cleaned up pcb. This chip is 30pins long (2 x15) and 11 pins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
  DHT11 Humitidy and Temperature Sensor (3 pins): DHT11 Humidity and Temperature Sensor (3 pins).
  PH meter with sensor in breadboard: analog ph sensor module.
  : TDS Meter V1.0 Development Board Water Meter Filter Measuring Water Sensor Module.
  1 chan 5v relay module: 1 Channel 5V Relay Module Board Shield with Optocoupler Support High and Low Level Trigger for Arduino.
  water pump/motor: WATER PUMP BY ARDUBLOCKTR
