# Fritzing sketch DHT11+DS18B20_ESP32 (saved by Fritzing 0.9.5d)
breadboards: 1

parts:
  DS2 = DS18B20 1-Wire Temperature Sensor Probe
  R3 = Resistor [tolerance=±5% resistance=4.7 package="2010 [SMD]"]
  VCC1 = Battery
  M2 = DOIT Esp32 DevKit v1 (30 pins long, 11 pins width) [part_number=ESP32S-PIN30]
  DHT1 = DHT11 Humitidy and Temperature Sensor (3 pins)

nets:
  GND: DS2.GND, VCC1.-, DHT1.Gnd
  N1: DS2.DQ, R3.Pin_1, M2.D13
  N2: DS2.VDD, R3.Pin_0, VCC1.+, DHT1.Signal
  N3: M2.D4, DHT1.Plus

custom parts:
  DOIT Esp32 DevKit v1 (30 pins long, 11 pins width): The DOIT Esp32 DevKit v1 is one of the development board created by DOIT to evaluate the ESP-WROOM-32 module. It is based on the ESP32 microcontroller that boasts Wifi, Bluetooth, Ethernet and Low Power support all in a single chip. (vanepp) made breadboard work, adjusted pin numbering and labels and reduced size of schematic and cleaned up pcb. This chip is 30pins long (2 x15) and 11 pins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
  DHT11 Humitidy and Temperature Sensor (3 pins): DHT11 Humidity and Temperature Sensor (3 pins).
