# Fritzing sketch LDR_ESP32 (saved by Fritzing 0.9.5d)
breadboards: 1

parts:
  VCC1 = Battery
  R5 = Resistor [tolerance=±5% resistance=10 package="2010 [SMD]"]
  R7 = Photocell (LDR) [package=THT]
  M3 = DOIT Esp32 DevKit v1 (30 pins long, 11 pins width) [part_number=ESP32S-PIN30]

nets:
  N1: VCC1.-, R5.Pin_1
  N2: VCC1.+, R7.pin_0
  N3: R5.Pin_0, R7.pin_1, M3.D34

custom parts:
  DOIT Esp32 DevKit v1 (30 pins long, 11 pins width): The DOIT Esp32 DevKit v1 is one of the development board created by DOIT to evaluate the ESP-WROOM-32 module. It is based on the ESP32 microcontroller that boasts Wifi, Bluetooth, Ethernet and Low Power support all in a single chip. (vanepp) made breadboard work, adjusted pin numbering and labels and reduced size of schematic and cleaned up pcb. This chip is 30pins long (2 x15) and 11 pins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
