# Fritzing sketch PH+TDS (saved by Fritzing 0.9.5d)
breadboards: 1

parts:
  M2 = PH meter with sensor in breadboard [package=THT]
  VCC1 = Battery
  A2 = tds-sensor-meter-v1.0_1
  M5 = DOIT Esp32 DevKit v1 (30 pins long, 11 pins width) [part_number=ESP32S-PIN30]

nets:
  N1: M2.pin1, VCC1.-, A2.pin3
  N2: M2.pin2, VCC1.+, A2.pin2
  N3: M2.pin3, M5.D35
  N4: A2.pin1, M5.D32

custom parts:
  PH meter with sensor in breadboard: analog ph sensor module.
  : TDS Meter V1.0 Development Board Water Meter Filter Measuring Water Sensor Module.
  DOIT Esp32 DevKit v1 (30 pins long, 11 pins width): The DOIT Esp32 DevKit v1 is one of the development board created by DOIT to evaluate the ESP-WROOM-32 module. It is based on the ESP32 microcontroller that boasts Wifi, Bluetooth, Ethernet and Low Power support all in a single chip. (vanepp) made breadboard work, adjusted pin numbering and labels and reduced size of schematic and cleaned up pcb. This chip is 30pins long (2 x15) and 11 pins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
