# Fritzing sketch Ultrasonic-ESP32CAM (saved by Fritzing 0.9.5d)
breadboards: 1

parts:
  HC-SR04_Sensor_1 = HC-SR04 Ultrasonic Distance Sensor
  VCC1 = Battery
  ESP32_-_Back1 = ESP32 - CAM

nets:
  VCC: HC-SR04_Sensor_1.VCC, VCC1.+, ESP32_-_Back1.5V
  N1: HC-SR04_Sensor_1.TRIG, ESP32_-_Back1.GPIO14
  N2: HC-SR04_Sensor_1.ECHO, ESP32_-_Back1.GPIO15
  GND: HC-SR04_Sensor_1.GND, VCC1.-, ESP32_-_Back1.GND

custom parts:
  ESP32 - CAM: The ESP32-CAM has a very competitive small-size camera module that can operate independently as a minimum system with a footprint of only 27*40.5*4.5mm and a deep sleep current of up to 6mA.
