# Fritzing sketch relay+water_motor (saved by Fritzing 0.9.5d)
breadboards: 1

parts:
  M1 = 1 chan 5v relay module
  WATER_PUMP1 = water pump/motor
  M6 = DOIT Esp32 DevKit v1 (30 pins long, 11 pins width) [part_number=ESP32S-PIN30]
  VCC1 = Battery

nets:
  N1: M1.pin_1, M1.pin_4, VCC1.+
  N2: M1.pin_2, WATER_PUMP1.pin_1, VCC1.-
  N3: M1.pin_3, M6.D26
  N4: M1.pin_5, WATER_PUMP1.pin_2

custom parts:
  1 chan 5v relay module: 1 Channel 5V Relay Module Board Shield with Optocoupler Support High and Low Level Trigger for Arduino.
  water pump/motor: WATER PUMP BY ARDUBLOCKTR
  DOIT Esp32 DevKit v1 (30 pins long, 11 pins width): The DOIT Esp32 DevKit v1 is one of the development board created by DOIT to evaluate the ESP-WROOM-32 module. It is based on the ESP32 microcontroller that boasts Wifi, Bluetooth, Ethernet and Low Power support all in a single chip. (vanepp) made breadboard work, adjusted pin numbering and labels and reduced size of schematic and cleaned up pcb. This chip is 30pins long (2 x15) and 11 pins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
